# Fritzing sketch diagram (saved by Fritzing 0.9.4)
breadboards: 1

parts:
  12v-to-3v = DC-DC CONVERTER [part_number=" dc-dc-converter" package=dc-dc_converter]
  powered_by_USB_wall_charger = ESP-WROOM-32 [ESP-32S] Module [part_number=ESP-WROOM-32]
  Alarm-exterior-siren-pins = screw terminal, 2 pins

nets:
  N1: 12v-to-3v.OUT-, powered_by_USB_wall_charger.GND
  N2: 12v-to-3v.OUT+, powered_by_USB_wall_charger.IO32
  N3: 12v-to-3v.IN-, Alarm-exterior-siren-pins.pin2
  N4: 12v-to-3v.IN+, Alarm-exterior-siren-pins.pin1

custom parts:
  DC-DC CONVERTER: WYHP 5A constant current/voltage manufactured by Shenzhen Weiyapuhua Technology Co., Ltd
  ESP-WROOM-32 [ESP-32S] Module: Espressif ESP-WROOM-32 WiFi/Bluetooth LE microcontroller module also known as the Ai-Thinker ESP-32S module with similar formfactor. The ESP32 is a microcontroller chip with WiFi and BLE capabilities. The chip is developed by Espressif and is the successor to the popular ESP8266 WiFi module.
